// Logisim project 2bit_adder.circ as structural Verilog: 1 circuit, main circuit main
module main (
  input  A0,
  input  B0,
  input  A1,
  input  B1,
  output S0,
  output S1,
  output Cout
);

  wire and_1_out, and_2_out, and_3_out, and_4_out, or_1_out, xor_1_out, xor_2_out;

  xor xor_1 (xor_1_out, A0, B0);
  xor xor_2 (xor_2_out, A1, B1);
  xor xor_3 (S0, xor_1_out, 1'b0);
  and and_1 (and_1_out, 1'b0, xor_1_out);
  and and_2 (and_2_out, B0, A0);
  xor xor_4 (S1, xor_2_out, or_1_out);
  and and_3 (and_3_out, or_1_out, xor_2_out);
  and and_4 (and_4_out, B1, A1);
  or or_1 (or_1_out, and_1_out, and_2_out);
  or or_2 (Cout, and_3_out, and_4_out);

  // Notes on the sheet:
  //   A0: Least significant digit of 2-bit number A
  //   A1:Most significant digit of 2-bit number A
  //   Cin to first adder set to 0
  //   B0: Least significant digit of 2-bit number B
  //   B1:Most significant digit of 2-bit number B
  //   Cout from first adder connected to Cin of second adder
endmodule
